# Fritzing sketch dfplayer (saved by Fritzing 0.9.3b)
breadboards: 1

parts:
  DFRobot_DFPlayer_Mini1 = DFRobot DFPlayer Mini [part_number=DFR0299]
  Part1 = Arduino Nano (Rev3.0) (ICSP)
  SP1 = SPEAKER [package=pcb_mount_speaker]
  R1 = Resistor [tolerance=±5% resistance=1k package="0603 [SMD]"]

nets:
  N1: DFRobot_DFPlayer_Mini1.RX, Part1.D1/TX, Part1.D0/RX, R1.Pin_0
  N2: DFRobot_DFPlayer_Mini1.TX, R1.Pin_1
  N3: DFRobot_DFPlayer_Mini1.SPK_1, SP1.-
  N4: DFRobot_DFPlayer_Mini1.GND-1, DFRobot_DFPlayer_Mini1.GND-2
  N5: DFRobot_DFPlayer_Mini1.SPK_2, SP1.+
